# Fritzing sketch O expansion (saved by Fritzing 0.9.3b)
circuit board: 0.778443cm x 7.15257cm
breadboards: 1

parts:
  OUT_Left = thonkiconn [package="PG203J [THT]"]
  IN_Left = thonkiconn [package="PG203J [THT]"]
  IN_Right = thonkiconn [package="PG203J [THT]"]
  OUT_Right = thonkiconn [package="PG203J [THT]"]
  OUTLGR-INRL = male pin header, 5 pins [form="♂ (male)"]

nets:
  N1: OUT_Left.signal, OUTLGR-INRL.pin1
  N2: OUT_Left.ground, IN_Left.ground, IN_Right.ground, OUT_Right.ground, OUTLGR-INRL.pin2
  N3: IN_Left.signal, OUTLGR-INRL.pin5
  N4: IN_Right.signal, OUTLGR-INRL.pin4
  N5: OUT_Right.signal, OUTLGR-INRL.pin3

custom parts:
  thonkiconn: mono switched Jack 3.5mm
