# Fritzing sketch 2HP Eurorack Panel Expander (saved by Fritzing 0.9.3b)
circuit board: 0.98cm x 12.7cm
breadboards: 1

parts:
  J1 = double row female pin header, 14 pins [form="♀ (female)"]
  Pad4 = Pad [width=9.4059304444444436 height=10.092200814814818 connect=center]
  Pad2 = Pad [width=6 height=9.0311111111111106 connect=center]
  Pad3 = Pad [width=6 height=9.0311111111111106 connect=center]
  Pad1 = Pad [width=6 height=9.0311111111111106 connect=center]
  Pad5 = Pad [width=3.5277777777777777 height=8.043333333333333 connect=center]

nets:
  N1: J1.pin3, Pad5.pad
  N2: J1.pin4, Pad1.pad
  N3: J1.pin9, Pad3.pad
  N4: J1.pin10, Pad4.pad
  N5: J1.pin11, Pad2.pad

notes:
  K_
  _-
