# Fritzing sketch Breakout Header Repeater (saved by Fritzing 0.9.3b)
circuit board: 8.46667cm x 5.64444cm
breadboards: 1

parts:
  J1 = double row female pin header, 14 pins [form="♀ (female)"]
  J2 = double row female pin header, 14 pins [form="♀ (female)"]

nets:
  N1: J1.pin1, J2.pin1
  N2: J1.pin2, J2.pin2
  N3: J1.pin3, J2.pin3
  N4: J1.pin4, J2.pin4
  N5: J1.pin5, J2.pin5
  N6: J1.pin6, J2.pin6
  N7: J1.pin7, J2.pin7
  N8: J1.pin8, J2.pin8
  N9: J1.pin9, J2.pin9
  N10: J1.pin10, J2.pin10
  N11: J1.pin11, J2.pin11
  N12: J1.pin12, J2.pin12
  N13: J1.pin13, J2.pin13
  N14: J1.pin14, J2.pin14
