# Fritzing sketch DIN MIDI Expander (saved by Fritzing 0.9.3b)
circuit board: 2cm x 4.5cm
breadboards: 1

parts:
  RLED = Resistor [tolerance=±5% resistance=220 package=THT]
  LED1 = LED - 5mm [color="Orange (605nm)" package="5 mm [THT]"]
  MIDI_OUT = DIN-5 jack (MIDI) [package=THT]
  MIDI_IN = DIN-5 jack (MIDI) [package=THT]
  R1 = Resistor [tolerance=±5% resistance=51 package=THT]
  Expander_Header = double row male pin header, 14 pins [form="♂ (male)"]
  R2 = Resistor [tolerance=±5% resistance=51 package=THT]
  6n137 = IC, DIP package, 8 pins [chip_label=IC]
  1n4148 = Diode [package=diode-1n4148]
  R3 = Resistor [tolerance=±5% resistance=220 package=THT]
  R4 = Resistor [tolerance=±5% resistance=10k package=THT]
  MIDI_Out_Wiring_Header = female pin header, 3 pins [form="♀ (female)"]
  MIDI_In_Header = female pin header, 2 pins [form="♀ (female)"]
  C1 = Ceramic Capacitor [capacitance=100nF package="100 mil [THT, multilayer]"]

nets:
  N1: RLED.Pin_0, LED1.anode
  N2: RLED.Pin_1, Expander_Header.pin12
  GND: LED1.cathode, MIDI_OUT.GND, Expander_Header.pin2, Expander_Header.pin13, 6n137.pin5, MIDI_Out_Wiring_Header.pin3, C1.0
  N3: MIDI_OUT.5, R1.Pin_0, MIDI_Out_Wiring_Header.pin1
  N4: MIDI_OUT.4, R2.Pin_0, MIDI_Out_Wiring_Header.pin2
  N5: MIDI_IN.5, 6n137.pin3, 1n4148.A, MIDI_In_Header.pin1
  N6: MIDI_IN.4, R3.Pin_0, MIDI_In_Header.pin2
  MIDI_Tx: R1.Pin_1, Expander_Header.pin10
  MIDI Rx: Expander_Header.pin6, 6n137.pin6, R4.Pin_1
  3.3V: Expander_Header.pin14, R2.Pin_1, 6n137.pin8, R4.Pin_0, C1.1
  N7: 6n137.pin2, 1n4148.C, R3.Pin_1

notes:
  1
  MIDI EXPANDER_002
