# Fritzing sketch DAC Version B 1.0.0.recoverfzz (saved by Fritzing 0.9.3b)
circuit board: 3.60489cm x 11.3038cm
breadboards: 1

parts:
  J3 = male pin header, 4 pins [form="♂ (male)"]
  J2 = male pin header, 5 pins [form="♂ (male)"]
  CV_in = female pin header, 5 pins [form="♀ (female)"]
  Q3 = TRANSISTOR_NPN [package=to-92]
  R5 = Resistor [tolerance=±5% resistance=100k package=THT]
  R6 = Resistor [tolerance=±5% resistance=33k package=THT]
  Q4 = TRANSISTOR_NPN [package=to-92]
  R7 = Resistor [tolerance=±5% resistance=100k package=THT]
  R8 = Resistor [tolerance=±5% resistance=33k package=THT]
  Q1 = TRANSISTOR_NPN [package=to-92]
  R1 = Resistor [tolerance=±5% resistance=100k package=THT]
  Q2 = TRANSISTOR_NPN [package=to-92]
  R3 = Resistor [tolerance=±5% resistance=100k package=THT]
  R4 = Resistor [tolerance=±5% resistance=33k package=THT]
  R25 = Resistor [tolerance=±5% resistance=100 package=THT]
  R26 = Resistor [tolerance=±5% resistance=100 package=THT]
  R27 = Resistor [tolerance=±5% resistance=100 package=THT]
  R28 = Resistor [tolerance=±5% resistance=100 package=THT]
  DAC1 = IC, DIP package, 14 pins [chip_label="DAC MCP4922"]
  DAC2 = IC, DIP package, 14 pins [chip_label="DAC MCP4922"]
  R2 = Resistor [tolerance=±5% resistance=33k package=THT]
  CV_Output_Buffer = MCP6004 [part_number=MCP6004 package="DIP (Dual Inline) [THT]"]
  Power_and_I2C_Header = double row male pin header, 8 pins [form="♂ (male)"]
  Eurorack_Power_Header = double row male pin header, 16 pins [form="♂ (male)"]
  3_3V = female pin header, 1 pin [form="♀ (female)"]
  Teensy_3_2 = Teensy 3.2 [part_number="Teensy 3.2"]
  Expander_Header = double row male pin header, 14 pins [form="♂ (male)"]  # not connected

nets (from the pcb view):
  N1: J3.pin1, CV_Output_Buffer.-IN_4, CV_Output_Buffer.Out_4
  N2: J3.pin2, CV_Output_Buffer.Out_3, CV_Output_Buffer.-IN_3
  N3: J3.pin3, CV_Output_Buffer.-IN_2, CV_Output_Buffer.Out_2
  N4: J3.pin4, CV_Output_Buffer.Out_1, CV_Output_Buffer.-IN_1
  N5: J2.pin1, Q3.E, R6.Pin_1, Q4.E, R8.Pin_1, Q1.E, Q2.E, R4.Pin_1, DAC1.pin8, DAC1.pin12, DAC2.pin8, DAC2.pin12, R2.Pin_1, Teensy_3_2.GND#16, Teensy_3_2.GND#49
  N6: J2.pin2, R7.Pin_0
  N7: J2.pin3, R5.Pin_0
  N8: J2.pin4, R3.Pin_0
  N9: J2.pin5, R1.Pin_0
  N10: CV_in.pin1, CV_Output_Buffer.Vdd(+)
  N11: CV_in.pin2, R28.Pin_0
  N12: CV_in.pin3, R27.Pin_0
  N13: CV_in.pin4, R26.Pin_0
  N14: CV_in.pin5, R25.Pin_0
  N15: Q3.B, R5.Pin_1, R6.Pin_0
  N16: Q3.C, Teensy_3_2.D3
  N17: Q4.B, R7.Pin_1, R8.Pin_0
  N18: Q4.C, Teensy_3_2.D0
  N19: Q1.B, R1.Pin_1, R2.Pin_0
  N20: Q1.C, Teensy_3_2.D4
  N21: Q2.B, R3.Pin_1, R4.Pin_0
  N22: Q2.C, Teensy_3_2.D5
  N23: R25.Pin_1, Teensy_3_2.A2/D16
  N24: R26.Pin_1, Teensy_3_2.A3/D17
  N25: R27.Pin_1, Teensy_3_2.A6/D20
  N26: R28.Pin_1, Teensy_3_2.A7/D21
  N27: DAC1.pin1, DAC1.pin9, DAC1.pin11, DAC1.pin13, DAC2.pin1, DAC2.pin9, DAC2.pin11, DAC2.pin13
  N28: DAC1.pin3, Teensy_3_2.D1
  N29: DAC1.pin4, DAC2.pin4, Teensy_3_2.A0/D14
  N30: DAC1.pin5, DAC2.pin5, Teensy_3_2.D7
  N31: DAC1.pin10, CV_Output_Buffer.+IN_2
  N32: DAC2.pin3, Teensy_3_2.D2
  N33: Power_and_I2C_Header.pin1, Power_and_I2C_Header.pin8, Eurorack_Power_Header.pin5, Eurorack_Power_Header.pin6, Eurorack_Power_Header.pin7, Eurorack_Power_Header.pin10, Eurorack_Power_Header.pin11, Eurorack_Power_Header.pin12, Teensy_3_2.AGND
  N34: Power_and_I2C_Header.pin2, Power_and_I2C_Header.pin7, Eurorack_Power_Header.pin3, Eurorack_Power_Header.pin14, Teensy_3_2.Vin
  N35: Power_and_I2C_Header.pin3, Power_and_I2C_Header.pin6, 3_3V.pin1, Teensy_3_2.3V3
  N36: Power_and_I2C_Header.pin4, Teensy_3_2.D30
  N37: Power_and_I2C_Header.pin5, Teensy_3_2.D29
  N38: Eurorack_Power_Header.pin1, Eurorack_Power_Header.pin16
  N39: Eurorack_Power_Header.pin2, Eurorack_Power_Header.pin15
  N40: Eurorack_Power_Header.pin4, Eurorack_Power_Header.pin13
  N41: Eurorack_Power_Header.pin8, Eurorack_Power_Header.pin9

notes:
  SAIC CV/MIDI/CV, B_1.0.0
  revB_1.0.0

custom parts:
  MCP6004: Quad Op-Amp with rail-to-rail output and low voltage operation
  Teensy 3.2: Updated from Fabian Althaus. The Teensy is a complete USB-based microcontoller development system, in a very small footprint, capable of implementing many types of projects. All programming is done via the USB port. No special programmer is needed, only a standard micro-USB cable and a PC or Macintosh with a USB port.
