# Fritzing sketch Interface_VersionB_1.0.1 (saved by Fritzing 0.9.3b)
circuit board: 3.60489cm x 11.3cm
breadboards: 1

parts:
  R1 = Rotary Potentiometer (Small) [maximum_resistance=100kΩ package=THT]
  R2 = Rotary Potentiometer (Small) [maximum_resistance=100kΩ package=THT]
  R4 = Rotary Potentiometer (Small) [maximum_resistance=100kΩ package=THT]
  R3 = Rotary Potentiometer (Small) [maximum_resistance=100kΩ package=THT]
  PJ3 = thonkiconn [package="PG203J [THT]"]
  PJ5 = thonkiconn [package="PG203J [THT]"]
  PJ6 = thonkiconn [package="PG203J [THT]"]
  PJ9 = thonkiconn [package="PG203J [THT]"]
  PJ10 = thonkiconn [package="PG203J [THT]"]
  PJ11 = thonkiconn [package="PG203J [THT]"]
  PJ12 = thonkiconn [package="PG203J [THT]"]
  PJ1 = thonkiconn [package="PG203J [THT]"]
  J3 = male pin header, 4 pins [form="♂ (male)"]
  PJ7 = thonkiconn [package="PG203J [THT]"]
  PJ2 = thonkiconnnoground [package="PG203J [THT]"]
  PJ4 = thonkiconnnoground [package="PG203J [THT]"]
  PJ8 = thonkiconnnoground [package="PG203J [THT]"]
  INPUT_SCALER = MCP6004 [part_number=MCP6004 package="DIP (Dual Inline) [THT]"]
  R25 = Resistor [tolerance=±5% resistance=100k package=THT]
  R26 = Resistor [tolerance=±5% resistance=100k package=THT]
  R27 = Resistor [tolerance=±5% resistance=100k package=THT]
  R28 = Resistor [tolerance=±5% resistance=100k package=THT]
  R29 = Resistor [tolerance=±5% resistance=66k package=THT]
  R30 = Resistor [tolerance=±5% resistance=66k package=THT]
  R31 = Resistor [tolerance=±5% resistance=66k package=THT]
  R32 = Resistor [tolerance=±5% resistance=66k package=THT]
  R33 = Resistor [tolerance=±5% resistance=66k package=THT]
  R34 = Resistor [tolerance=±5% resistance=66k package=THT]
  R35 = Resistor [tolerance=±5% resistance=66k package=THT]
  R36 = Resistor [tolerance=±5% resistance=66k package=THT]
  R37 = Resistor [tolerance=±5% resistance=100k package=THT]
  R38 = Resistor [tolerance=±5% resistance=100k package=THT]
  R39 = Resistor [tolerance=±5% resistance=100k package=THT]
  R40 = Resistor [tolerance=±5% resistance=100k package=THT]
  USB_Breakout = female pin header, 5 pins [form="♀ (female)"]  # not connected
  J1 = male pin header, 5 pins [form="♂ (male)"]
  J2 = male pin header, 5 pins [form="♂ (male)"]
  3_3V = female pin header, 1 pin [form="♀ (female)"]

nets:
  GND: R1.leg1, R2.leg1, R4.leg1, R3.leg1, PJ3.ground, PJ5.ground, PJ6.ground, PJ9.ground, PJ10.ground, PJ11.ground, PJ1.ground, PJ7.ground, INPUT_SCALER.Vss(GND), R29.Pin_1, R30.Pin_1, R31.Pin_1, R32.Pin_1, R37.Pin_1, R38.Pin_1, R39.Pin_0, R40.Pin_0, J2.pin5
  N1: R1.wiper, PJ5.signal
  N2: R1.leg2, R26.Pin_1
  N3: R2.wiper, PJ6.signal
  N4: R2.leg2, R25.Pin_1
  N5: R4.wiper, PJ8.signal
  N6: R4.leg2, R28.Pin_1
  N7: R3.wiper, PJ7.signal
  N8: R3.leg2, R27.Pin_1
  N9: PJ3.signal, J2.pin2
  5V: PJ5.switch, PJ6.switch, PJ7.switch, PJ8.switch, J1.pin1
  N10: PJ9.signal, J3.pin4
  N11: PJ10.signal, J3.pin3
  N12: PJ11.signal, J3.pin2
  N13: PJ12.signal, J3.pin1
  N14: PJ1.signal, J2.pin4
  N15: PJ2.signal, J2.pin3
  N16: PJ4.signal, J2.pin1
  CV 1: INPUT_SCALER.Out_1, R36.Pin_0, J1.pin5
  N17: INPUT_SCALER.-IN_1, R36.Pin_1, R39.Pin_1
  N18: INPUT_SCALER.+IN_1, R28.Pin_0, R29.Pin_0
  3.3V: INPUT_SCALER.Vdd(+), 3_3V.pin1
  N19: INPUT_SCALER.+IN_2, R27.Pin_0, R32.Pin_0
  N20: INPUT_SCALER.-IN_2, R35.Pin_0, R40.Pin_1
  CV 2: INPUT_SCALER.Out_2, R35.Pin_1, J1.pin4
  CV 3: INPUT_SCALER.Out_3, R34.Pin_1, J1.pin3
  N21: INPUT_SCALER.-IN_3, R34.Pin_0, R38.Pin_0
  N22: INPUT_SCALER.+IN_3, R25.Pin_0, R31.Pin_0
  N23: INPUT_SCALER.+IN_4, R26.Pin_0, R30.Pin_0
  N24: INPUT_SCALER.-IN_4, R33.Pin_1, R37.Pin_0
  CV 4: INPUT_SCALER.Out_4, R33.Pin_0, J1.pin2

notes:
  SAIC CV/MIDI/CV, B_1.0.0

custom parts:
  thonkiconn: mono switched Jack 3.5mm
  thonkiconnnoground: mono switched Jack 3.5mm
  MCP6004: Quad Op-Amp with rail-to-rail output and low voltage operation
