# Fritzing sketch DAC Version B 1.0.4_Fill (saved by Fritzing 0.9.3b)
circuit board: 3.60489cm x 11.1345cm
breadboards: 1

parts:
  CV_Out = male pin header, 4 pins [form="♂ (male)"]
  J2 = male pin header, 5 pins [form="♂ (male)"]
  Q3 = TRANSISTOR_NPN [package=to-92]
  R5 = Resistor [tolerance=±5% resistance=100k package=THT]
  R6 = Resistor [tolerance=±5% resistance=33k package=THT]
  Q4 = TRANSISTOR_NPN [package=to-92]
  R7 = Resistor [tolerance=±5% resistance=100k package=THT]
  R8 = Resistor [tolerance=±5% resistance=33k package=THT]
  Q1 = TRANSISTOR_NPN [package=to-92]
  R1 = Resistor [tolerance=±5% resistance=100k package=THT]
  Q2 = TRANSISTOR_NPN [package=to-92]
  R3 = Resistor [tolerance=±5% resistance=100k package=THT]
  R4 = Resistor [tolerance=±5% resistance=33k package=THT]
  R25 = Resistor [tolerance=±5% resistance=100 package=THT]
  R26 = Resistor [tolerance=±5% resistance=100 package=THT]
  R27 = Resistor [tolerance=±5% resistance=100 package=THT]
  R28 = Resistor [tolerance=±5% resistance=100 package=THT]
  DAC1 = IC, DIP package, 14 pins [chip_label="DAC MCP4922"]
  DAC2 = IC, DIP package, 14 pins [chip_label="DAC MCP4922"]
  R2 = Resistor [tolerance=±5% resistance=33k package=THT]
  Power_and_I2C_Header = double row male pin header, 8 pins [form="♂ (male)"]
  Eurorack_Power_Header = double row male pin header, 16 pins [form="♂ (male)"]
  Teensy_3_2 = Teensy 3.2 [part_number="Teensy 3.2"]
  Expander_Header = double row male pin header, 14 pins [form="♂ (male)"]
  Interface_Pots = female pin header, 5 pins [form="♀ (female)"]
  CV_Output_Buffer = MCP6004 [part_number=MCP6004 package="DIP (Dual Inline) [THT]"]
  5V_Euro = male pin header, 3 pins [form="♂ (male)"]
  R_LED = Resistor [tolerance=±5% resistance=220 package=THT]
  LED1 = LED - 5mm [color="Red (633nm)" package="5 mm [THT]"]
  CV_in = female pin header, 5 pins [form="♀ (female)"]
  J3 = female pin header, 14 pins [form="♀ (female)"]
  J4 = female pin header, 14 pins [form="♀ (female)"]  # not connected
  J5 = female pin header, 3 pins [form="♀ (female)"]  # not connected
  J6 = female pin header, 5 pins [form="♀ (female)"]
  J8 = female pin header, 7 pins [form="♀ (female)"]  # not connected
  J7 = female pin header, 7 pins [form="♀ (female)"]

nets:
  N1: CV_Out.pin1, CV_Output_Buffer.-IN_2, CV_Output_Buffer.Out_2
  N2: CV_Out.pin2, CV_Output_Buffer.Out_3, CV_Output_Buffer.-IN_3
  N3: CV_Out.pin3, CV_Output_Buffer.Out_1, CV_Output_Buffer.-IN_1
  N4: CV_Out.pin4, CV_Output_Buffer.-IN_4, CV_Output_Buffer.Out_4
  GND: J2.pin1, Q3.E, R6.Pin_1, Q4.E, R8.Pin_1, Q1.E, Q2.E, R4.Pin_1, DAC1.pin8, DAC1.pin12, DAC2.pin8, DAC2.pin12, R2.Pin_1, Power_and_I2C_Header.pin1, Power_and_I2C_Header.pin8, Eurorack_Power_Header.pin5, Eurorack_Power_Header.pin6, Eurorack_Power_Header.pin7, Eurorack_Power_Header.pin10, Eurorack_Power_Header.pin11, Eurorack_Power_Header.pin12, Teensy_3_2.GND#16, Teensy_3_2.GND#49, Expander_Header.pin2, Expander_Header.pin13, CV_Output_Buffer.Vss(GND), LED1.cathode
  N5: J2.pin2, R7.Pin_0
  N6: J2.pin3, R5.Pin_0
  N7: J2.pin4, R3.Pin_0
  N8: J2.pin5, R1.Pin_0
  N9: Q3.B, R5.Pin_1, R6.Pin_0
  TRIG 3: Q3.C, Teensy_3_2.D3
  N10: Q4.B, R7.Pin_1, R8.Pin_0
  TRIG 4: Q4.C, Teensy_3_2.D0
  N11: Q1.B, R1.Pin_1, R2.Pin_0
  TRIG 1: Q1.C, Teensy_3_2.D4
  N12: Q2.B, R3.Pin_1, R4.Pin_0
  TRIG 2: Q2.C, Teensy_3_2.D5
  N13: R25.Pin_0, CV_in.pin5
  N14: R25.Pin_1, Teensy_3_2.A2/D16
  N15: R26.Pin_0, CV_in.pin4
  N16: R26.Pin_1, Teensy_3_2.A3/D17
  N17: R27.Pin_0, CV_in.pin3
  N18: R27.Pin_1, Teensy_3_2.A6/D20
  N19: R28.Pin_0, CV_in.pin2
  N20: R28.Pin_1, Teensy_3_2.A7/D21
  5V: DAC1.pin1, DAC1.pin9, DAC1.pin11, DAC1.pin13, DAC2.pin1, DAC2.pin9, DAC2.pin11, DAC2.pin13, Power_and_I2C_Header.pin2, Power_and_I2C_Header.pin7, Teensy_3_2.Vin, CV_Output_Buffer.Vdd(+), 5V_Euro.pin1, J3.pin14
  N21: DAC1.pin3, Teensy_3_2.D1
  SCK: DAC1.pin4, DAC2.pin4, Teensy_3_2.A0/D14, J3.pin2
  MOSI: DAC1.pin5, DAC2.pin5, Teensy_3_2.D7
  CV OUT B: DAC1.pin10, CV_Output_Buffer.+IN_2
  CV OUT A: DAC1.pin14, CV_Output_Buffer.+IN_1
  N22: DAC2.pin3, Teensy_3_2.D2
  CV OUT D: DAC2.pin10, CV_Output_Buffer.+IN_4
  CV OUT C: DAC2.pin14, CV_Output_Buffer.+IN_3
  3.3V: Power_and_I2C_Header.pin3, Power_and_I2C_Header.pin6, Teensy_3_2.3V3, Expander_Header.pin14, Interface_Pots.pin1
  N23: Power_and_I2C_Header.pin4, Teensy_3_2.D30, J7.pin2
  N24: Power_and_I2C_Header.pin5, Teensy_3_2.D29, J7.pin1
  N25: Eurorack_Power_Header.pin1, Eurorack_Power_Header.pin16
  N26: Eurorack_Power_Header.pin2, Eurorack_Power_Header.pin15
  N27: Eurorack_Power_Header.pin3, Eurorack_Power_Header.pin14, 5V_Euro.pin2
  N28: Eurorack_Power_Header.pin4, Eurorack_Power_Header.pin13
  N29: Eurorack_Power_Header.pin8, Eurorack_Power_Header.pin9
  N30: Teensy_3_2.D8, Expander_Header.pin12, R_LED.Pin_0
  N31: Teensy_3_2.D24, Expander_Header.pin5
  N32: Teensy_3_2.D25, Expander_Header.pin9
  N33: Teensy_3_2.D26, Expander_Header.pin6
  N34: Teensy_3_2.D27, Expander_Header.pin8
  N35: Teensy_3_2.D28, Expander_Header.pin7
  N36: Teensy_3_2.D31, Expander_Header.pin10
  N37: Teensy_3_2.A12, Interface_Pots.pin5
  N38: Teensy_3_2.A13, Interface_Pots.pin4
  N39: Teensy_3_2.A11, Interface_Pots.pin3
  N40: Teensy_3_2.A10, Interface_Pots.pin2
  N41: Expander_Header.pin3, J6.pin5
  N42: Expander_Header.pin4, J7.pin4
  N43: Expander_Header.pin11, J7.pin5
  N44: R_LED.Pin_1, LED1.anode

notes:
  revB_1.0.4
  SAIC CV/MIDI/CV, 1.0.2

custom parts:
  Teensy 3.2: Updated from Fabian Althaus. The Teensy is a complete USB-based microcontoller development system, in a very small footprint, capable of implementing many types of projects. All programming is done via the USB port. No special programmer is needed, only a standard micro-USB cable and a PC or Macintosh with a USB port.
  MCP6004: Quad Op-Amp with rail-to-rail output and low voltage operation
