# Fritzing sketch Interface_VersionB_1.0.5_Filled (saved by Fritzing 0.9.3b)
circuit board: 3.60489cm x 11.173cm
breadboards: 1

parts:
  R1 = Rotary Potentiometer (Small) [maximum_resistance=100kΩ package=THT]
  R2 = Rotary Potentiometer (Small) [maximum_resistance=100kΩ package=THT]
  R4 = Rotary Potentiometer (Small) [maximum_resistance=100kΩ package=THT]
  R3 = Rotary Potentiometer (Small) [maximum_resistance=100kΩ package=THT]
  PJ3 = thonkiconn [package="PG203J [THT]"]
  PJ5 = thonkiconn [package="PG203J [THT]"]
  PJ6 = thonkiconn [package="PG203J [THT]"]
  PJ9 = thonkiconn [package="PG203J [THT]"]
  PJ10 = thonkiconn [package="PG203J [THT]"]
  PJ11 = thonkiconn [package="PG203J [THT]"]
  PJ12 = thonkiconn [package="PG203J [THT]"]
  PJ1 = thonkiconn [package="PG203J [THT]"]
  PJ7 = thonkiconn [package="PG203J [THT]"]
  PJ2 = thonkiconnnoground [package="PG203J [THT]"]
  PJ4 = thonkiconnnoground [package="PG203J [THT]"]
  INPUT_SCALER = MCP6004 [part_number=MCP6004 package="DIP (Dual Inline) [THT]"]
  R25 = Resistor [tolerance=±5% resistance=100k package=THT]
  R26 = Resistor [tolerance=±5% resistance=100k package=THT]
  R27 = Resistor [tolerance=±5% resistance=100k package=THT]
  R28 = Resistor [tolerance=±5% resistance=100k package=THT]
  R29 = Resistor [tolerance=±5% resistance=66k package=THT]
  R30 = Resistor [tolerance=±5% resistance=66k package=THT]
  R31 = Resistor [tolerance=±5% resistance=66k package=THT]
  R32 = Resistor [tolerance=±5% resistance=66k package=THT]
  R33 = Resistor [tolerance=±5% resistance=66k package=THT]
  R34 = Resistor [tolerance=±5% resistance=66k package=THT]
  R35 = Resistor [tolerance=±5% resistance=66k package=THT]
  R36 = Resistor [tolerance=±5% resistance=66k package=THT]
  R37 = Resistor [tolerance=±5% resistance=100k package=THT]
  R38 = Resistor [tolerance=±5% resistance=100k package=THT]
  R39 = Resistor [tolerance=±5% resistance=100k package=THT]
  R40 = Resistor [tolerance=±5% resistance=100k package=THT]
  PJ8 = thonkiconnnoground [package="PG203J [THT]"]
  USB_Breakout = double row female pin header, 10 pins [form="♀ (female)"]
  RLED = Resistor [tolerance=±5% resistance=220 package=THT]
  LED1 = LED - 5mm [color="Red (633nm)" package="5 mm [THT]"]
  J2 = male pin header, 5 pins [form="♂ (male)"]
  P = male pin header, 5 pins [form="♂ (male)"]
  CV_IN_HEADER = male pin header, 5 pins [form="♂ (male)"]
  CV_OUT_HEADER = male pin header, 4 pins [form="♂ (male)"]
  J3 = female pin header, 5 pins [form="♀ (female)"]

nets:
  GND: R1.leg1, R2.leg1, R4.leg1, R3.leg1, PJ3.ground, PJ5.switch, PJ5.ground, PJ6.switch, PJ6.ground, PJ9.ground, PJ10.ground, PJ11.ground, PJ12.ground, PJ1.ground, PJ7.switch, PJ7.ground, INPUT_SCALER.Vss(GND), R29.Pin_1, R30.Pin_1, R31.Pin_1, R32.Pin_1, R37.Pin_1, R38.Pin_1, R39.Pin_0, R40.Pin_0, PJ8.switch, LED1.cathode, J2.pin5, J3.pin1
  N1: R1.wiper, P.pin5
  3.3V: R1.leg2, R2.leg2, R4.leg2, R3.leg2, INPUT_SCALER.Vdd(+), P.pin1
  N2: R2.wiper, P.pin4
  N3: R4.wiper, P.pin2
  N4: R3.wiper, P.pin3
  N5: PJ3.signal, J2.pin2, J3.pin4
  N6: PJ5.signal, R26.Pin_1
  N7: PJ6.signal, R25.Pin_1
  N8: PJ9.signal, CV_OUT_HEADER.pin4
  N9: PJ10.signal, CV_OUT_HEADER.pin3
  N10: PJ11.signal, CV_OUT_HEADER.pin2
  N11: PJ12.signal, CV_OUT_HEADER.pin1
  N12: PJ1.signal, J2.pin4, J3.pin2
  N13: PJ7.signal, R27.Pin_1
  N14: PJ2.signal, J2.pin3, J3.pin3
  N15: PJ4.signal, J2.pin1, J3.pin5
  CV 1: INPUT_SCALER.Out_1, R36.Pin_0, CV_IN_HEADER.pin5
  N16: INPUT_SCALER.-IN_1, R36.Pin_1, R39.Pin_1
  N17: INPUT_SCALER.+IN_1, R28.Pin_0, R29.Pin_0
  N18: INPUT_SCALER.+IN_2, R27.Pin_0, R32.Pin_0
  N19: INPUT_SCALER.-IN_2, R35.Pin_0, R40.Pin_1
  CV 2: INPUT_SCALER.Out_2, R35.Pin_1, CV_IN_HEADER.pin4
  CV 3: INPUT_SCALER.Out_3, R34.Pin_1, CV_IN_HEADER.pin3
  N20: INPUT_SCALER.-IN_3, R34.Pin_0, R38.Pin_0
  N21: INPUT_SCALER.+IN_3, R25.Pin_0, R31.Pin_0
  N22: INPUT_SCALER.+IN_4, R26.Pin_0, R30.Pin_0
  N23: INPUT_SCALER.-IN_4, R33.Pin_1, R37.Pin_0
  CV 4: INPUT_SCALER.Out_4, R33.Pin_0, CV_IN_HEADER.pin2
  N24: R28.Pin_1, PJ8.signal
  N25: USB_Breakout.pin1, USB_Breakout.pin10
  N26: USB_Breakout.pin2, USB_Breakout.pin9
  N27: USB_Breakout.pin3, USB_Breakout.pin8
  N28: USB_Breakout.pin4, USB_Breakout.pin7
  N29: USB_Breakout.pin5, USB_Breakout.pin6
  N30: RLED.Pin_0, LED1.anode
  5V: RLED.Pin_1, CV_IN_HEADER.pin1

notes:
  SAIC CV/MIDI/CV, 1.0.2
  REVB_1.0.5

custom parts:
  thonkiconn: mono switched Jack 3.5mm
  thonkiconnnoground: mono switched Jack 3.5mm
  MCP6004: Quad Op-Amp with rail-to-rail output and low voltage operation
